# Fritzing sketch pir (saved by Fritzing 0.9.2b)
circuit board: 8.46667cm x 5.64444cm
breadboards: 1

parts:
  PIR1 = PIR sensor
  Parte1 = Arduino Uno (Rev3)
  R1 = Resistor [tolerance=±5% resistance=220 package=THT]

nets:
  VDD: PIR1.VDD, Parte1.5V, R1.Pin_1
  GND: PIR1.GND, Parte1.GND
  N1: PIR1.AL, Parte1.D2, R1.Pin_0
