# Fritzing sketch expressions (saved by Fritzing 0.9.2b)
circuit board: 8.46667cm x 5.64444cm
perfboards: 1
breadboards: 1

parts:
  Arduino1 = Arduino Uno (Rev3)
  LED_4 = LED - 5mm [color="Yellow (585nm)" package="5 mm [THT]"]
  LED_7 = LED - 5mm [color="Yellow (585nm)" package="5 mm [THT]"]
  LED_8 = LED - 5mm [color="Yellow (585nm)" package="5 mm [THT]"]
  LED_6 = LED - 5mm [color="Yellow (585nm)" package="5 mm [THT]"]
  LED_5 = LED - 5mm [color="Yellow (585nm)" package="5 mm [THT]"]
  LED_3 = LED - 5mm [color="Yellow (585nm)" package="5 mm [THT]"]
  LED_1 = LED - 5mm [color="Yellow (585nm)" package="5 mm [THT]"]
  LED_2 = LED - 5mm [color="Yellow (585nm)" package="5 mm [THT]"]
  R4 = Resistor [tolerance=±5% resistance=220 package=THT]
  R7 = Resistor [tolerance=±5% resistance=220 package=THT]
  R8 = Resistor [tolerance=±5% resistance=220 package=THT]
  R6 = Resistor [tolerance=±5% resistance=220 package=THT]
  R3 = Resistor [tolerance=±5% resistance=220 package=THT]
  R1 = Resistor [tolerance=±5% resistance=220 package=THT]
  R2 = Resistor [tolerance=±5% resistance=220 package=THT]
  U3 = 74HC595 [package="DIP16 [THT]"]
  R5 = Resistor [tolerance=±5% resistance=220 package=THT]

nets:
  N1: Arduino1.D8, U3.DS
  N2: Arduino1.D12/MISO, U3.ST_CP
  GND: Arduino1.GND, LED_4.cathode, LED_7.cathode, LED_8.cathode, LED_6.cathode, LED_5.cathode, LED_3.cathode, LED_1.cathode, LED_2.cathode, U3.GND
  N3: Arduino1.D7, U3.SH_CP
  5V: Arduino1.5V, U3.MR, U3.VCC
  N4: LED_4.anode, R4.Pin_1
  N5: LED_7.anode, R7.Pin_0
  N6: LED_8.anode, R8.Pin_0
  N7: LED_6.anode, R6.Pin_0
  N8: LED_5.anode, R5.Pin_0
  N9: LED_3.anode, R3.Pin_1
  N10: LED_1.anode, R1.Pin_1
  N11: LED_2.anode, R2.Pin_1
  N12: R4.Pin_0, U3.Q3
  N13: R7.Pin_1, U3.Q6
  N14: R8.Pin_1, U3.Q7
  N15: R6.Pin_1, U3.Q5
  N16: R3.Pin_0, U3.Q2
  N17: R1.Pin_0, U3.Q0
  N18: R2.Pin_0, U3.Q1
  N19: U3.Q4, R5.Pin_1
