# Fritzing sketch sensor_ultrasonidos_hc_sr04 (saved by Fritzing 0.9.2b)

parts:
  Parte1 = SRF05 Ultrasonic Rangefinder
  Parte2 = Arduino Uno (Rev3)

nets:
  VCC: Parte1.VCC, Parte2.5V
  N1: Parte1.Trig, Parte2.D12/MISO
  N2: Parte1.Echo, Parte2.D11_PWM/MOSI
  GND: Parte1.GND, Parte2.GND
