# Fritzing sketch emisor_ir (saved by Fritzing 0.9.2b)
circuit board: 8.46667cm x 5.64444cm

parts:
  Arduino = Arduino Uno (Rev3)
  Emisor_IR = LED - 5mm [color="Infrared (940nm)" package="5 mm [THT]"]
  Resistencia = Resistor [tolerance=±5% resistance=220 package=THT]

nets:
  N1: Arduino.GND, Emisor_IR.cathode
  N2: Arduino.D3_PWM, Resistencia.Pin_1
  N3: Emisor_IR.anode, Resistencia.Pin_0

// code stored in the sketch: arduino-example-emisor-ir.ino
/****************************************/
/************ EMISOR INFRARROJOS ***********/
/****************************************/
/* Autor: Diego de los Reyes Rodríguez. */
/****************************************/

#include <IRLib.h>
#include <IRLibMatch.h>
#include <IRLibTimer.h>
#include <ComunicacionIR.h>

IRsend _emisor; 
String datos = "";

void setup() {
  Serial.begin(9600);
  Serial.println("ENVIANDO DATOS");
}

void loop() {
  _emisor.send(NEC, 0xE0E040BF, 32);
  delay(300);
}
