# Fritzing sketch receptor_ir (saved by Fritzing 0.9.2b)

parts:
  Arduino = Arduino Uno (Rev3)
  Resistencia = Resistor [tolerance=±5% resistance=220 package=THT]
  IR1 = TSOP312.., 314.. [package=THT]

nets:
  N1: Arduino.D8, Resistencia.Pin_1
  N2: Arduino.5V, IR1.Vs
  GND: Arduino.GND, IR1.GND
  N3: Resistencia.Pin_0, IR1.Data

// code stored in the sketch: arduino-example-receptor-ir.ino
/****************************************/
/************ ECO INFRARROJOS ***********/
/****************************************/
/* Autor: Diego de los Reyes Rodríguez. */
/****************************************/

#include <IRLib.h>
#include <IRLibMatch.h>
#include <IRLibTimer.h>

/** VARIABLES **/

//Recibe IR.
IRrecv receptor(8);//Use input pin 11

//Decodifica un valor recibido.
IRdecode decodificador;

//Último protocolo recibido.
IRTYPES protocolo = UNKNOWN;

//Último código recibido.
unsigned long codigo;

//Orden recibida por el puerto serial.
int orden = 0;

/** FUNCIONES ARDUINO **/

/**
 * Se ejecuta al arrancar el programa.
 */
void setup()
{
  Serial.begin(9600) ;
  receptor.enableIRIn(); // Start the receiver
  Serial.println("Receptor IR.") ;
}

/**
 * Bucle infinito de ejecución.
 */
void loop()
{
  if (receptor.GetResults(&decodificador)) {	
    decodificador.decode();//decode the signal	
    if(decodificador.decode_type != UNKNOWN && decodificador.value != 0xFFFFFFFF){
      codigo = decodificador.value;
      protocolo = decodificador.decode_type;
      Serial.println("RECIBIDO");
  		Serial.print("Protocolo: ");
  		Serial.println(Pnames(protocolo));
  		Serial.print("Valor: ");
  		Serial.println(codigo, HEX);
    }	
    receptor.resume(); //restart the receiver	
  }
	delay(300);
}
