# Fritzing sketch led-matrix (saved by Fritzing 0.9.3b)

parts:
  Componente2 = Arduino Uno (Rev3)
  8x8_LED_Modul_mit_MAX1 = 8x8 LED Modul mit MAX7219 [package=THT]

nets:
  N1: Componente2.D10_PWM/SS, 8x8_LED_Modul_mit_MAX1.CS_Eingang
  N2: Componente2.D11_PWM/MOSI, 8x8_LED_Modul_mit_MAX1.CLK_Eingang
  N3: Componente2.D12/MISO, 8x8_LED_Modul_mit_MAX1.DIN_Eingang
  N4: Componente2.GND, 8x8_LED_Modul_mit_MAX1.GND_Eingang
  N5: Componente2.5V, 8x8_LED_Modul_mit_MAX1.VCC_Eingang
