# Fritzing sketch schema (saved by Fritzing 0.9.3b)

parts:
  Componente1 = Arduino Uno (Rev3)
  Raspberry_Pi_1 = Raspberry Pi 3 [part_number=RPI-3-V1.2]

nets:
  N1: Componente1.D0/RX, Raspberry_Pi_1.GPIO14
  N2: Componente1.D1/TX, Raspberry_Pi_1.GPIO15
  GND: Componente1.GND, Raspberry_Pi_1.GND
  VIN: Componente1.VIN, Raspberry_Pi_1.5V
